// Logisim project BeEight.circ as structural Verilog: 1 circuit, main circuit main
module main (
);

  wire ADD, AddressMode, ALUop, CMP, demultiplexer_1_out0, demultiplexer_1_out1, demultiplexer_1_out2,
       demultiplexer_1_out3, demultiplexer_1_out4, demultiplexer_1_out5, demultiplexer_1_out6,
       demultiplexer_1_out7, JP, JPC, LD, NANDinst, not_1_out, ST, STP;
  wire [6:0] PrimBuffer_q;
  wire [7:0] Accumulator_q, adder_1_out, ALUout, Databus, nand_1_out, SecBuffer_q, SecBufferIn;
  wire [11:0] ProgramCounter_q, ProgramCounterStorage_q;

  Register #(.width(12)) ProgramCounterStorage (
    .D(ProgramCounter_q), .Q(ProgramCounterStorage_q));  // open: en, clk, clr
  Counter #(.max('hfff), .width(12)) ProgramCounter (
    .D(ProgramCounterStorage_q), .Q(ProgramCounter_q));  // open: clr, load, up, count, clk, carry
  ROM #(.addrWidth(12)) Memory (.addr(ProgramCounter_q), .data(Databus));
  Register PrimBuffer (.Q({AddressMode, PrimBuffer_q}));  // open: D, en, clk, clr
  assign SecBufferIn = not_1_out ? Databus : 8'bz;  // Controlled_Buffer controlled_buffer_1
  not not_1 (not_1_out, ALUop);
  assign SecBufferIn = ALUop ? ALUout : 8'bz;  // Controlled_Buffer controlled_buffer_2
  Demultiplexer #(.select(3)) demultiplexer_1 (
    .out0(demultiplexer_1_out0), .out1(demultiplexer_1_out1), .out2(demultiplexer_1_out2),
    .out3(demultiplexer_1_out3), .out4(demultiplexer_1_out4), .out5(demultiplexer_1_out5),
    .out6(demultiplexer_1_out6), .out7(demultiplexer_1_out7), .in(1'b1), .sel(PrimBuffer_q[6:4]));
  // Probe on PrimBuffer_q[6:4]
  Register SecBuffer (.D(SecBufferIn), .Q(SecBuffer_q));  // open: en, clk, clr
  not not_2 (LD, demultiplexer_1_out0);
  not not_3 (ST, demultiplexer_1_out1);
  not not_4 (ADD, demultiplexer_1_out2);
  not not_5 (NANDinst, demultiplexer_1_out3);
  not not_6 (CMP, demultiplexer_1_out4);
  not not_7 (STP, demultiplexer_1_out5);
  not not_8 (JP, demultiplexer_1_out6);
  not not_9 (JPC, demultiplexer_1_out7);
  Register Accumulator (.D(SecBuffer_q), .Q(Accumulator_q));  // open: en, clk, clr
  Counter #(.max('hf), .width(4)) counter_1 ();  // open: clr, load, up, count, clk, D, carry, Q
  D_Flip_Flop ConditionalFlag ();  // open: D, clk, Q, Qn, preset, reset
  or or_1 (ALUop, ADD, NANDinst);
  Adder adder_1 (.a(Accumulator_q), .b(SecBuffer_q), .out(adder_1_out));  // open: cin, cout
  assign nand_1_out = ~(Accumulator_q & SecBuffer_q);  // NAND_Gate nand_1, 8 bits wide
  Register ALUbuffer (.D(adder_1_out), .Q(ALUout));  // open: en, clk, clr

  // Notes on the sheet:
  //   contents of Memory (hex, n*v repeats v):
  //   0 37 86 66 96 65 20 10 a6 65 30 18 b5 55
endmodule
